# Fritzing sketch blinkende_led (saved by Fritzing 1.0.1rc)
breadboards: 1

parts:
  LED1 = LED - 5mm [color="Red (633nm)" current=0.030 package="5 mm [THT]"]
  Bauteil1 = Arduino Uno (Rev3)
  R1 = Resistor [tolerance=±5% power=0.25 resistance=200 package=THT]

nets:
  N1: LED1.cathode, Bauteil1.GND
  N2: LED1.anode, R1.Pin_0
  N3: Bauteil1.D12/MISO, R1.Pin_1

// code stored in the sketch: Untitled.ino
void setup() {
	pinMode(12, OUTPUT);
}

void loop() {
	digitalWrite(12, HIGH);
	delay(1000);
	digitalWrite(12, LOW);
	delay(1000);
}
