# Fritzing sketch led_taster (saved by Fritzing 1.0.1rc)
breadboards: 1

parts:
  Bauteil1 = Arduino Uno (Rev3)
  R1 = Resistor [tolerance=±5% power=0.25 resistance=200 package=THT]
  LED1 = LED - 5mm [color="Red (633nm)" current=0.030 package="5 mm [THT]"]
  S1 = Pushbutton [package="[THT]"]

nets:
  N1: Bauteil1.D11_PWM/MOSI, R1.Pin_1
  N2: Bauteil1.D12/MISO, S1.Pin_1, S1.Pin_2
  N3: Bauteil1.GND, LED1.cathode, S1.Pin_3, S1.Pin_4
  N4: R1.Pin_0, LED1.anode

// code stored in the sketch: Untitled.ino

