# Fritzing sketch pwm_poti (saved by Fritzing 1.0.1rc)
breadboards: 1

parts:
  Bauteil1 = Arduino Uno (Rev3)
  R1 = Resistor [tolerance=±5% power=0.25 resistance=200 package=THT]
  LED1 = LED - 5mm [color="Red (633nm)" current=0.030 package="5 mm [THT]"]
  R2 = Rotary Potentiometer (Small) [maximum_resistance=100kΩ knob_status=50% package=THT]

nets:
  N1: Bauteil1.A0, R2.wiper
  N2: Bauteil1.D9_PWM, R1.Pin_1
  N3: Bauteil1.5V, R2.leg2
  N4: Bauteil1.GND, LED1.cathode, R2.leg1
  N5: R1.Pin_0, LED1.anode
