# Fritzing sketch ldr (saved by Fritzing 1.0.1rc)
breadboards: 1

parts:
  Bauteil1 = Arduino Uno (Rev3)
  R1 = Resistor [tolerance=±5% power=0.25 resistance=200 package=THT]
  LED1 = LED - 5mm [color="Red (633nm)" current=0.030 package="5 mm [THT]"]
  R2 = Photocell (LDR) [package=THT]
  R3 = Resistor [tolerance=±5% power=0.25 resistance=10k package=THT]

nets:
  N1: Bauteil1.A0, R2.pin_1, R3.Pin_0
  N2: Bauteil1.D9_PWM, R1.Pin_1
  N3: Bauteil1.5V, R3.Pin_1
  N4: Bauteil1.GND, LED1.cathode, R2.pin_0
  N5: R1.Pin_0, LED1.anode
