# Fritzing sketch buzzer (saved by Fritzing 1.0.1rc)
breadboards: 1

parts:
  Bauteil1 = Arduino Uno (Rev3)
  S1 = Pushbutton [package="[THT]"]
  J1 = Piezo Speaker

nets:
  N1: Bauteil1.D11_PWM/MOSI, J1.pin2
  N2: Bauteil1.D12/MISO, S1.Pin_1, S1.Pin_2
  N3: Bauteil1.GND, S1.Pin_3, S1.Pin_4, J1.pin1

// code stored in the sketch: Untitled.ino

